// Digital circuit 74xx00.sff.dig as structural Verilog
module _74xx00_sff (
  input  in_2,
  input  in_3,
  output out_1
);

  wire nand_1_out, nand_2_out, nand_4_out;

  nand nand_1 (nand_1_out, in_3, in_2);
  nand nand_2 (nand_2_out, nand_1_out, in_2);
  nand nand_3 (out_1, nand_1_out, nand_4_out);
  nand nand_4 (nand_4_out, out_1, nand_2_out);

  // Notes on the sheet:
  //   out_1: pin 2
  //   in_2: pin 1
endmodule
