// Digital circuit 74xx181_1bit.dig as structural Verilog
module _74xx181_1bit (
  input  in_1,
  input  in_2,
  input  in_3,
  input  in_4,
  input  in_5,
  input  in_6,
  input  in_7,
  input  in_8,
  output out_9
);

  wire and_1_out, and_2_out, and_3_out, and_4_out, and_5_out, and_6_out, and_7_out, nand_1_out, nor_1_out,
       nor_2_out, nor_3_out, not_1_out, not_2_out, xor_1_out;

  not not_1 (not_1_out, in_5);
  and and_1 (and_1_out, in_4, in_5);
  and and_2 (and_2_out, in_3, not_1_out);
  and and_3 (and_3_out, not_1_out, in_2);
  and and_4 (and_4_out, in_5, in_1);
  and and_5 (and_5_out, in_6, in_6);
  and and_6 (and_6_out, and_1_out, in_6);
  and and_7 (and_7_out, and_2_out, in_6);
  nor nor_1 (nor_1_out, and_3_out, and_4_out);
  nor nor_2 (nor_2_out, and_6_out, and_7_out);
  nor nor_3 (nor_3_out, nor_1_out, and_5_out);
  not not_2 (not_2_out, in_7);
  xor xor_1 (xor_1_out, nor_2_out, nor_3_out);
  nand nand_1 (nand_1_out, not_2_out, in_8);
  // _7400 _7400_1: pin names not known
  xor xor_2 (out_9, xor_1_out, nand_1_out);
endmodule
