// Digital circuit compar.dig as structural Verilog
module compar (
  input  in_4,
  input  in_5,
  input  in_6,
  input  in_7,
  output out_1,
  output out_2,
  output out_3,
  output out_8,
  output out_9,
  output out_10
);

  wire nand_1_out, not_1_out, not_2_out;

  not not_1 (not_1_out, in_4);
  not not_2 (not_2_out, in_5);
  and and_1 (out_2, not_1_out, in_5);
  and and_2 (out_3, in_4, not_2_out);
  xnor xnor_1 (out_1, out_2, out_3);
  nand nand_1 (nand_1_out, in_6, in_7);
  nand nand_2 (out_9, in_6, nand_1_out);
  nand nand_3 (out_10, nand_1_out, in_7);
  nand nand_4 (out_8, out_9, out_10);
endmodule
